// Digital circuit BCDadder.dig as structural Verilog
module BCDadder (
  input  [3:0] A,
  input  [3:0] B,
  input  Cin,
  output [3:0] Sum,
  output Cout
);

  wire decoder_1_out_10, decoder_1_out_11, decoder_1_out_12, decoder_1_out_13, decoder_1_out_14,
       decoder_1_out_15, xor_1_out;
  wire [1:0] _4bitripplecarryadder_1_carry;
  wire [3:0] _4bitripplecarryadder_1_sum, _4bitripplecarryadder_2_sum;

  _4BitRippleCarryAdder _4bitripplecarryadder_1 (
    .A(A), .B(B), .Cin(Cin), .CARRY(_4bitripplecarryadder_1_carry[1]), .SUM(_4bitripplecarryadder_1_sum));
  Decoder #(.Selector_Bits(4)) decoder_1 (
    .sel(_4bitripplecarryadder_1_sum), .out_10(decoder_1_out_10), .out_11(decoder_1_out_11),
    .out_12(decoder_1_out_12), .out_13(decoder_1_out_13), .out_14(decoder_1_out_14), .out_15(decoder_1_out_15));  // open: out_0, out_1, out_2, out_3, out_4, out_5, out_6, out_7, out_8, out_9
  or or_1 (_4bitripplecarryadder_1_carry[0], decoder_1_out_10, decoder_1_out_11, decoder_1_out_12, decoder_1_out_13, decoder_1_out_14, decoder_1_out_15);
  xor xor_1 (xor_1_out, _4bitripplecarryadder_1_carry[0], 1'b1);
  _4BitRippleCarryAdder _4bitripplecarryadder_2 (
    .A(_4bitripplecarryadder_1_sum), .B(4'b0110), .Cin(1'b0), .SUM(_4bitripplecarryadder_2_sum));  // open: CARRY
  Multiplexer #(.Bits(4)) multiplexer_1 (
    .sel(_4bitripplecarryadder_1_carry[0]), .in_0(_4bitripplecarryadder_1_sum),
    .in_1(_4bitripplecarryadder_2_sum), .out(Sum));
  Multiplexer #(.Selector_Bits(2)) multiplexer_2 (
    .sel(_4bitripplecarryadder_1_carry), .in_0(_4bitripplecarryadder_1_carry[0]),
    .in_1(_4bitripplecarryadder_1_carry[0]), .in_2(xor_1_out), .in_3(_4bitripplecarryadder_1_carry[0]),
    .out(Cout));
endmodule
