// Digital circuit calculator.dig as structural Verilog
module calculator (
  input  [3:0] DATA,
  input  DA,
  input  CLK,
  output [3:0] D0,
  output [3:0] D1,
  output [3:0] D2,
  output [3:0] D3,
  output [3:0] D4,
  output [3:0] D5,
  output [3:0] D6,
  output [3:0] D7
);

  wire and_1_out, bcdadder_1_cout, bcdadder_2_cout, bcdadder_3_cout, bcdadder_4_cout, bcdadder_5_cout,
       bcdadder_6_cout, bcdadder_7_cout, d_ff_1_nq, decoder_1_out_14, decoder_1_out_15, or_1_out;
  wire [3:0] bcdadder_1_sum, bcdadder_2_sum, bcdadder_3_sum, bcdadder_4_sum, bcdadder_5_sum, bcdadder_6_sum,
       bcdadder_7_sum, bcdadder_8_sum, multiplexer_1_out, multiplexer_2_out, multiplexer_3_out,
       multiplexer_4_out, multiplexer_6_out, multiplexer_7_out, multiplexer_8_out, multiplexer_9_out,
       multiplexer_11_out, multiplexer_12_out, multiplexer_13_out, multiplexer_14_out, multiplexer_16_out,
       multiplexer_17_out, multiplexer_18_out, multiplexer_19_out, multiplexer_21_out, multiplexer_22_out,
       multiplexer_23_out, multiplexer_24_out, multiplexer_26_out, multiplexer_27_out, multiplexer_28_out,
       multiplexer_29_out, multiplexer_30_out, multiplexer_32_out, multiplexer_33_out, multiplexer_34_out,
       multiplexer_36_out, multiplexer_37_out, multiplexer_38_out, register_1_q, register_2_q, register_3_q,
       register_4_q, register_5_q, register_6_q, register_7_q, register_8_q, register_9_q, register_10_q,
       register_11_q, register_12_q, register_13_q, register_14_q, register_15_q, register_16_q;

  Decoder #(.Selector_Bits(4)) decoder_1 (
    .sel(DATA), .out_14(decoder_1_out_14), .out_15(decoder_1_out_15));  // open: out_0, out_1, out_2, out_3, out_4, out_5, out_6, out_7, out_8, out_9, out_10, out_11, out_12, out_13
  D_FF d_ff_1 (.D(DA), .C(CLK), .nQ(d_ff_1_nq));  // open: Q
  and and_1 (and_1_out, DA, d_ff_1_nq);
  Multiplexer #(.Bits(4)) multiplexer_1 (
    .sel(decoder_1_out_14), .in_0(bcdadder_1_sum), .in_1(4'b0000), .out(multiplexer_1_out));
  Register #(.Bits(4)) register_1 (.D(multiplexer_1_out), .C(CLK), .en(and_1_out), .Q(register_1_q));
  or or_1 (or_1_out, decoder_1_out_14, decoder_1_out_15);
  BCDadder bcdadder_1 (
    .A(register_1_q), .B(multiplexer_2_out), .Cin(1'b0), .Sum(bcdadder_1_sum), .Cout(bcdadder_1_cout));
  Multiplexer #(.Bits(4)) multiplexer_2 (
    .sel(decoder_1_out_15), .in_0(4'b0000), .in_1(register_2_q), .out(multiplexer_2_out));
  Register #(.Bits(4)) register_2 (.D(multiplexer_3_out), .C(CLK), .en(and_1_out), .Q(register_2_q));
  Multiplexer #(.Bits(4)) multiplexer_3 (.sel(or_1_out), .in_0(DATA), .in_1(4'b0000), .out(multiplexer_3_out));
  Multiplexer #(.Bits(4)) multiplexer_4 (.sel(and_1_out), .in_0(4'b0000), .in_1(register_2_q), .out(multiplexer_4_out));
  Multiplexer #(.Bits(4)) multiplexer_5 (.sel(decoder_1_out_15), .in_0(register_2_q), .in_1(bcdadder_1_sum), .out(D0));
  Multiplexer #(.Bits(4)) multiplexer_6 (
    .sel(decoder_1_out_14), .in_0(bcdadder_2_sum), .in_1(4'b0000), .out(multiplexer_6_out));
  BCDadder bcdadder_2 (
    .A(register_4_q), .B(multiplexer_7_out), .Cin(bcdadder_1_cout), .Sum(bcdadder_2_sum),
    .Cout(bcdadder_2_cout));
  Multiplexer #(.Bits(4)) multiplexer_7 (
    .sel(decoder_1_out_15), .in_0(4'b0000), .in_1(register_3_q), .out(multiplexer_7_out));
  Register #(.Bits(4)) register_3 (.D(multiplexer_8_out), .C(CLK), .en(and_1_out), .Q(register_3_q));
  Multiplexer #(.Bits(4)) multiplexer_8 (
    .sel(or_1_out), .in_0(multiplexer_4_out), .in_1(4'b0000), .out(multiplexer_8_out));
  Register #(.Bits(4)) register_4 (.D(multiplexer_6_out), .C(CLK), .en(and_1_out), .Q(register_4_q));
  Multiplexer #(.Bits(4)) multiplexer_9 (.sel(and_1_out), .in_0(4'b0000), .in_1(register_3_q), .out(multiplexer_9_out));
  Multiplexer #(.Bits(4)) multiplexer_10 (.sel(decoder_1_out_15), .in_0(register_3_q), .in_1(bcdadder_2_sum), .out(D1));
  Multiplexer #(.Bits(4)) multiplexer_11 (
    .sel(decoder_1_out_14), .in_0(bcdadder_3_sum), .in_1(4'b0000), .out(multiplexer_11_out));
  Multiplexer #(.Bits(4)) multiplexer_12 (
    .sel(decoder_1_out_15), .in_0(4'b0000), .in_1(register_5_q), .out(multiplexer_12_out));
  Register #(.Bits(4)) register_5 (.D(multiplexer_13_out), .C(CLK), .en(and_1_out), .Q(register_5_q));
  Multiplexer #(.Bits(4)) multiplexer_13 (
    .sel(or_1_out), .in_0(multiplexer_9_out), .in_1(4'b0000), .out(multiplexer_13_out));
  Register #(.Bits(4)) register_6 (.D(multiplexer_11_out), .C(CLK), .en(and_1_out), .Q(register_6_q));
  BCDadder bcdadder_3 (
    .A(register_6_q), .B(multiplexer_12_out), .Cin(bcdadder_2_cout), .Sum(bcdadder_3_sum),
    .Cout(bcdadder_3_cout));
  Multiplexer #(.Bits(4)) multiplexer_14 (
    .sel(and_1_out), .in_0(4'b0000), .in_1(register_5_q), .out(multiplexer_14_out));
  Multiplexer #(.Bits(4)) multiplexer_15 (.sel(decoder_1_out_15), .in_0(register_5_q), .in_1(bcdadder_3_sum), .out(D2));
  Multiplexer #(.Bits(4)) multiplexer_16 (
    .sel(decoder_1_out_14), .in_0(bcdadder_4_sum), .in_1(4'b0000), .out(multiplexer_16_out));
  Multiplexer #(.Bits(4)) multiplexer_17 (
    .sel(decoder_1_out_15), .in_0(4'b0000), .in_1(register_7_q), .out(multiplexer_17_out));
  Register #(.Bits(4)) register_7 (.D(multiplexer_18_out), .C(CLK), .en(and_1_out), .Q(register_7_q));
  Multiplexer #(.Bits(4)) multiplexer_18 (
    .sel(or_1_out), .in_0(multiplexer_14_out), .in_1(4'b0000), .out(multiplexer_18_out));
  Register #(.Bits(4)) register_8 (.D(multiplexer_16_out), .C(CLK), .en(and_1_out), .Q(register_8_q));
  BCDadder bcdadder_4 (
    .A(register_8_q), .B(multiplexer_17_out), .Cin(bcdadder_3_cout), .Sum(bcdadder_4_sum),
    .Cout(bcdadder_4_cout));
  Multiplexer #(.Bits(4)) multiplexer_19 (
    .sel(and_1_out), .in_0(4'b0000), .in_1(register_7_q), .out(multiplexer_19_out));
  Multiplexer #(.Bits(4)) multiplexer_20 (.sel(decoder_1_out_15), .in_0(register_7_q), .in_1(bcdadder_4_sum), .out(D3));
  Multiplexer #(.Bits(4)) multiplexer_21 (
    .sel(decoder_1_out_14), .in_0(bcdadder_5_sum), .in_1(4'b0000), .out(multiplexer_21_out));
  Multiplexer #(.Bits(4)) multiplexer_22 (
    .sel(decoder_1_out_15), .in_0(4'b0000), .in_1(register_9_q), .out(multiplexer_22_out));
  Register #(.Bits(4)) register_9 (.D(multiplexer_23_out), .C(CLK), .en(and_1_out), .Q(register_9_q));
  Register #(.Bits(4)) register_10 (.D(multiplexer_21_out), .C(CLK), .en(and_1_out), .Q(register_10_q));
  BCDadder bcdadder_5 (
    .A(register_10_q), .B(multiplexer_22_out), .Cin(bcdadder_4_cout), .Sum(bcdadder_5_sum),
    .Cout(bcdadder_5_cout));
  Multiplexer #(.Bits(4)) multiplexer_23 (
    .sel(or_1_out), .in_0(multiplexer_19_out), .in_1(4'b0000), .out(multiplexer_23_out));
  Multiplexer #(.Bits(4)) multiplexer_24 (
    .sel(and_1_out), .in_0(4'b0000), .in_1(register_9_q), .out(multiplexer_24_out));
  Multiplexer #(.Bits(4)) multiplexer_25 (.sel(decoder_1_out_15), .in_0(register_9_q), .in_1(bcdadder_5_sum), .out(D4));
  Multiplexer #(.Bits(4)) multiplexer_26 (
    .sel(decoder_1_out_14), .in_0(bcdadder_6_sum), .in_1(4'b0000), .out(multiplexer_26_out));
  Multiplexer #(.Bits(4)) multiplexer_27 (
    .sel(decoder_1_out_15), .in_0(4'b0000), .in_1(register_11_q), .out(multiplexer_27_out));
  Register #(.Bits(4)) register_11 (.D(multiplexer_28_out), .C(CLK), .en(and_1_out), .Q(register_11_q));
  Register #(.Bits(4)) register_12 (.D(multiplexer_26_out), .C(CLK), .en(and_1_out), .Q(register_12_q));
  BCDadder bcdadder_6 (
    .A(register_12_q), .B(multiplexer_27_out), .Cin(bcdadder_5_cout), .Sum(bcdadder_6_sum),
    .Cout(bcdadder_6_cout));
  Multiplexer #(.Bits(4)) multiplexer_28 (
    .sel(or_1_out), .in_0(multiplexer_24_out), .in_1(4'b0000), .out(multiplexer_28_out));
  Multiplexer #(.Bits(4)) multiplexer_29 (
    .sel(and_1_out), .in_0(4'b0000), .in_1(register_11_q), .out(multiplexer_29_out));
  Multiplexer #(.Bits(4)) multiplexer_30 (
    .sel(decoder_1_out_15), .in_0(4'b0000), .in_1(register_13_q), .out(multiplexer_30_out));
  Register #(.Bits(4)) register_13 (.D(multiplexer_33_out), .C(CLK), .en(and_1_out), .Q(register_13_q));
  Multiplexer #(.Bits(4)) multiplexer_31 (
    .sel(decoder_1_out_15), .in_0(register_11_q), .in_1(bcdadder_6_sum), .out(D5));
  Multiplexer #(.Bits(4)) multiplexer_32 (
    .sel(decoder_1_out_14), .in_0(bcdadder_7_sum), .in_1(4'b0000), .out(multiplexer_32_out));
  BCDadder bcdadder_7 (
    .A(register_14_q), .B(multiplexer_30_out), .Cin(bcdadder_6_cout), .Sum(bcdadder_7_sum),
    .Cout(bcdadder_7_cout));
  Multiplexer #(.Bits(4)) multiplexer_33 (
    .sel(or_1_out), .in_0(multiplexer_29_out), .in_1(4'b0000), .out(multiplexer_33_out));
  Register #(.Bits(4)) register_14 (.D(multiplexer_32_out), .C(CLK), .en(and_1_out), .Q(register_14_q));
  Multiplexer #(.Bits(4)) multiplexer_34 (
    .sel(and_1_out), .in_0(4'b0000), .in_1(register_13_q), .out(multiplexer_34_out));
  Multiplexer #(.Bits(4)) multiplexer_35 (
    .sel(decoder_1_out_15), .in_0(register_13_q), .in_1(bcdadder_7_sum), .out(D6));
  Multiplexer #(.Bits(4)) multiplexer_36 (
    .sel(decoder_1_out_14), .in_0(bcdadder_8_sum), .in_1(4'b0000), .out(multiplexer_36_out));
  BCDadder bcdadder_8 (
    .A(register_16_q), .B(multiplexer_37_out), .Cin(bcdadder_7_cout), .Sum(bcdadder_8_sum));  // open: Cout
  Multiplexer #(.Bits(4)) multiplexer_37 (
    .sel(decoder_1_out_15), .in_0(4'b0000), .in_1(register_15_q), .out(multiplexer_37_out));
  Register #(.Bits(4)) register_15 (.D(multiplexer_38_out), .C(CLK), .en(and_1_out), .Q(register_15_q));
  Multiplexer #(.Bits(4)) multiplexer_38 (
    .sel(or_1_out), .in_0(multiplexer_34_out), .in_1(4'b0000), .out(multiplexer_38_out));
  Register #(.Bits(4)) register_16 (.D(multiplexer_36_out), .C(CLK), .en(and_1_out), .Q(register_16_q));
  Multiplexer #(.Bits(4)) multiplexer_39 (
    .sel(decoder_1_out_15), .in_0(register_15_q), .in_1(bcdadder_8_sum), .out(D7));
endmodule
